# Fritzing sketch led (saved by Fritzing 0.9.3b)
breadboards: 1

parts:
  Raspberry_Pi_1 = Raspberry Pi 3 [part_number=RPI-3-V1.2]
  LED1 = smd LED [color="Red (633nm)" package="0805 [SMD]"]  # not connected
  R1 = Resistor [tolerance=±5% resistance=220 package="0402 [SMD]"]

nets:
  N1: Raspberry_Pi_1.GPIO2, Raspberry_Pi_1.GPIO3, Raspberry_Pi_1.GPIO4
  N2: Raspberry_Pi_1.GPIO11, R1.Pin_1

notes:
  Rasberry PI 3
  Protoboard (Breadbord)
  LED
  PIN 25
  GND (Terra)
  PIN 7
  Resistor
